// Logisim project simplified_logic.circ as structural Verilog: 1 circuit, main circuit main
module main (
  input  C,
  input  B,
  input  A,
  output AB_prime,
  output C___AB_prime,
  output A_prime___B,
  output C_prime_A_prime___B___prime
);

  wire and_2_out, not_1_out, not_2_out, not_3_out;

  not not_1 (not_1_out, B);
  not not_2 (not_2_out, A);
  and and_1 (AB_prime, A, not_1_out);
  or or_1 (A_prime___B, not_2_out, B);
  not not_3 (not_3_out, C);
  or or_2 (C___AB_prime, AB_prime, C);
  not not_4 (C_prime_A_prime___B___prime, and_2_out);
  and and_2 (and_2_out, A_prime___B, not_3_out);

  // Notes on the sheet:
  //   => f(ABC) = C + AB'
  //   f(ABC) = ABC + A'BC + AB'C'+AB'C+A'B'C = BC(A+A') + AB'(C+C') + A'B'C = BC(1) + AB'(1) + A'B'C = BC + B'(A+AC)
  //   = BC + B'((A+A')(A+C)) = BC + B'(1(A+C+) = BC + B'(A+C) = BC + AB' + B'C = (B+B')C + AB' = C(1) = AB' = C + AB'
  //   NAND form
endmodule
